# Fritzing sketch fleek (saved by Fritzing 0.9.2b)

parts:
  R6 = Resistor [tolerance=±5% resistance=100 package="0805 [SMD]"]
  R7 = Resistor [tolerance=±5% resistance=100 package="0805 [SMD]"]
  R8 = Resistor [tolerance=±5% resistance=100 package="0805 [SMD]"]
  LED1 = LEDs [package=led10mm]
  LED2 = LEDs [package=led10mm]
  LED3 = LEDs [package=led10mm]
  J1 = Piezo Speaker
  R9 = Resistor [tolerance=±5% resistance=1k package="1206 [SMD]"]
  Part1 = Arduino ProtoShield
  S1 = Pushbutton [package="[THT]"]
  R11 = Resistor [tolerance=±5% resistance=10k package=THT]
  R12 = Resistor [tolerance=±5% resistance=10k package=THT]
  R13 = Resistor [tolerance=±5% resistance=10k package=THT]
  S2 = Pushbutton [package="[THT]"]
  S3 = Pushbutton [package="[THT]"]
  J2 = Infrared Proximity Sensor

nets:
  N1: R6.Pin_0, LED3.C, Part1.N$107
  N2: R6.Pin_1, Part1.D7
  N3: R7.Pin_0, LED2.C, Part1.N$118
  N4: R7.Pin_1, Part1.D8
  N5: R8.Pin_0, LED1.C, Part1.N$129
  N6: R8.Pin_1, Part1.D9
  GND: LED1.A, LED2.A, LED3.A, Part1.GND, Part1.N$132, J2.GND
  N7: J1.pin1, R9.Pin_0, Part1.N$30
  N8: J1.pin2, Part1.D3
  N9: Part1.D4, Part1.N$68
  5V: Part1.D5, Part1.5V, Part1.N$67, Part1.N$79, Part1.N$89, Part1.N$143, S1.Pin_3, S1.Pin_4, R11.Pin_0, S2.Pin_3, S2.Pin_4, S3.Pin_3, S3.Pin_4, J2.Vcc
  N10: Part1.D6, Part1.N$90
  N11: Part1.A0, Part1.N$121, J2.Vout
  N12: Part1.N$69, R12.Pin_0
  N13: Part1.N$92, R13.Pin_0
